# Fritzing sketch ProCraftVolanteEsquemaArquino1.0 (saved by Fritzing 0.9.4)
breadboards: 1

parts:
  Part1 = Arduino Uno (Rev3)
  R1 = Rotary Potentiometer (Small) [maximum_resistance=100kΩ package=THT]
  Freio = Momentary Switch [package=ksa_sealed_tac_switch]
  Acelerador = Momentary Switch [package=ksa_sealed_tac_switch]
  R2 = Resistor [tolerance=±5% resistance=220 package="1206 [SMD]"]
  R3 = Resistor [tolerance=±5% resistance=220 package="1206 [SMD]"]
  R4 = Resistor [tolerance=±5% resistance=220 package="1206 [SMD]"]

nets:
  N1: Part1.A0, R4.Pin_1
  N2: Part1.D8, Freio.3
  N3: Part1.D7, Acelerador.3
  N4: Part1.GND, R1.leg1, R2.Pin_1
  N5: R1.wiper, R4.Pin_0
  N6: Freio.2, R2.Pin_0
  N7: Acelerador.2, R3.Pin_0
